# Fritzing sketch esp8266-Electra-AC (saved by Fritzing 0.9.5d)
breadboards: 1

parts:
  WeMos_D1_Mini1 = WeMos D1 Mini
  D1 = LTE-302 [package=lte-302]
  Q2 = NPN-Transistor [package="TO92 [THT]"]
  A1 = AHT10 module
  Mod1 = KY-022 Infrared Receiver Module [package="Breakout board"]
  R1 = Resistor [tolerance=±5% resistance=220 package=THT]

nets:
  5V: WeMos_D1_Mini1.5V, D1.A, A1.Pin_4, Mod1.Vin
  N1: WeMos_D1_Mini1.D1, A1.Pin_2
  N2: WeMos_D1_Mini1.D2, A1.Pin_1
  N3: WeMos_D1_Mini1.D5, Mod1.S
  N4: WeMos_D1_Mini1.D6, R1.Pin_1
  N5: WeMos_D1_Mini1.G, Q2.E, A1.Pin_3, Mod1.-
  N6: D1.C, Q2.C
  N7: Q2.B, R1.Pin_0

custom parts:
  AHT10 module: AHT10 Temperature Humidity Sensor Measurement Module High-Precision Digital Temp Humidity Sensor Measurement Module 1.8-6.0V I2C.
  KY-022 Infrared Receiver Module: KY-022 IR receiver module, reacts to 38kHz infrared light.
